# Fritzing sketch water_counter_02 (saved by Fritzing 0.9.4)
breadboards: 1

parts:
  WeMos_D1_Mini1 = WeMos D1 Mini
  PIR1 = PIR sensor
  OLED1 = OLED 128x64 I2C Monochrome Display
  Part1 = Real Time Clock Module - DS1307 RTC Breakout Board
  S4 = Pushbutton [package="[THT]"]
  S5 = Pushbutton [package="[THT]"]
  R1 = Resistor [tolerance=±5% resistance=220 package="1206 [SMD]"]
  TP1 = TTP223 Touch Module [part_number=TTP223]
  TP2 = TTP223 Touch Module [part_number=TTP223]
  TP3 = TTP223 Touch Module [part_number=TTP223]

nets:
  VCC: WeMos_D1_Mini1.5V, PIR1.VDD, OLED1.VDD, Part1.5V, TP1.VCC, TP2.VCC, TP3.VCC
  N1: WeMos_D1_Mini1.D0, PIR1.GND
  N2: WeMos_D1_Mini1.D1, Part1.SCL
  N3: WeMos_D1_Mini1.D2, Part1.SDA
  N4: WeMos_D1_Mini1.D3, S5.Pin_1, S5.Pin_2
  N5: WeMos_D1_Mini1.D4, S4.Pin_1, S4.Pin_2
  N6: WeMos_D1_Mini1.D5, TP2.I/O
  N7: WeMos_D1_Mini1.D6, TP1.I/O
  N8: WeMos_D1_Mini1.D7, TP3.I/O
  GND: WeMos_D1_Mini1.G, PIR1.SIG, OLED1.GND, S4.Pin_3, S4.Pin_4, S5.Pin_3, S5.Pin_4, R1.Pin_0, TP1.GND, TP2.GND, TP3.GND
  N9: Part1.GND, R1.Pin_1

custom parts:
  TTP223 Touch Module: Single touch module. Other side has "A" "B" terminal to short and use "AHLB" & "Toggle" Mode.
